// Logisim project 16_bit_CPU.circ as structural Verilog: 6 circuits, main circuit project_alu
module project_alu (
  input  [15:0] A,
  input  [15:0] B,
  input  [3:0] AUSel,
  input  [2:0] RUSel,
  output [15:0] AUResult,
  output [15:0] AUDout,
  output RUResult
);

  project_ao project_ao_1 (.A(A), .B(B), .AUSel(AUSel), .AUResult(AUDout));
  project_ro project_ro_1 (.A(A), .B(B), .RUSel(RUSel), .RUResult(RUResult));

  assign AUResult = AUDout;
endmodule

module project_ao (
  input  [15:0] A,
  input  [15:0] B,
  input  [3:0] AUSel,
  output [15:0] AUResult
);

  wire [15:0] adder_1_out, and_1_out, divider_1_out, divider_1_rem, multiplier_1_out, negator_1_out,
       negator_2_out, or_1_out, shifter_1_out, shifter_2_out, shifter_3_out, shifter_4_out, subtractor_1_out,
       xor_1_out;

  Adder #(.width(16)) adder_1 (.a(A), .b(B), .out(adder_1_out));  // open: cin, cout
  assign and_1_out = A & B;  // AND_Gate and_1, 16 bits wide
  assign or_1_out = A | B;  // OR_Gate or_1, 16 bits wide
  assign xor_1_out = A ^ B;  // XOR_Gate xor_1, 16 bits wide
  Divider #(.width(16)) divider_1 (.a(A), .b(B), .out(divider_1_out), .rem(divider_1_rem));  // open: upper
  Multiplier #(.width(16)) multiplier_1 (.a(A), .b(B), .out(multiplier_1_out));  // open: cin, cout
  Subtractor #(.width(16)) subtractor_1 (.a(A), .b(B), .out(subtractor_1_out));  // open: bin, bout
  Shifter #(.width(16)) shifter_1 (.in(A), .\dist (4'b0010), .out(shifter_1_out));
  Shifter #(.width(16)) shifter_2 (.in(B), .\dist (4'b0010), .out(shifter_2_out));
  Shifter #(.shift("lr"), .width(16)) shifter_3 (.in(A), .\dist (4'b0010), .out(shifter_3_out));
  Shifter #(.shift("lr"), .width(16)) shifter_4 (.in(B), .\dist (4'b0010), .out(shifter_4_out));
  Negator #(.width(16)) negator_1 (.in(A), .out(negator_1_out));
  Negator #(.width(16)) negator_2 (.in(B), .out(negator_2_out));
  Multiplexer #(.select(4), .width(16)) multiplexer_1 (
    .in0(adder_1_out), .in1(and_1_out), .in2(or_1_out), .in3(xor_1_out), .in4(divider_1_out),
    .in5(divider_1_rem), .in6(multiplier_1_out), .in7(subtractor_1_out), .in8(shifter_1_out),
    .in9(shifter_2_out), .in10(shifter_3_out), .in11(shifter_4_out), .in12(negator_1_out),
    .in13(negator_2_out), .out(AUResult), .sel(AUSel));  // open: in14, in15
endmodule

module project_ro (
  input  [15:0] A,
  input  [15:0] B,
  input  [2:0] RUSel,
  output RUResult
);

  wire comparator_1_eq, comparator_1_gt, comparator_1_lt, not_1_out, or_1_out, or_2_out;

  or or_1 (or_1_out, comparator_1_gt, comparator_1_eq);
  Comparator #(.width(16)) comparator_1 (
    .a(A), .b(B), .gt(comparator_1_gt), .eq(comparator_1_eq), .lt(comparator_1_lt));
  or or_2 (or_2_out, comparator_1_lt, comparator_1_eq);
  not not_1 (not_1_out, comparator_1_eq);
  Multiplexer #(.select(3)) multiplexer_1 (
    .in0(comparator_1_gt), .in1(comparator_1_eq), .in2(or_1_out), .in3(comparator_1_lt), .in4(or_2_out),
    .in5(not_1_out), .out(RUResult), .sel(RUSel));  // open: in6, in7
endmodule

module project_register_16 (
  input  [15:0] input_val,
  input  WE,
  input  clk,
  input  reset,
  input  OE,
  output [15:0] result,
  output [15:0] Dout,
  output [7:0] Eight_LSB,
  output [7:0] Eight_MSB
);

  Register #(.width(16)) register_1 (.D(input_val), .en(WE), .clk(clk), .Q(result), .clr(reset));
  assign Dout = OE ? result : 16'bz;  // Controlled_Buffer controlled_buffer_1
  BitSelector #(.group(8), .width(16)) bitselector_1 (.in(Dout), .out(Eight_LSB), .sel(1'b0));
  BitSelector #(.group(8), .width(16)) bitselector_2 (.in(Dout), .out(Eight_MSB), .sel(1'b1));
endmodule

module project_register_8 (
  input  [7:0] input_val,
  input  WE,
  input  clk,
  input  reset,
  input  OE,
  output [7:0] result,
  output [7:0] Dout,
  output [3:0] Eight_LSB,
  output [3:0] Eight_MSB
);

  Register register_1 (.D(input_val), .en(WE), .clk(clk), .Q(result), .clr(reset));
  assign Dout = OE ? result : 8'bz;  // Controlled_Buffer controlled_buffer_1
  BitSelector #(.group(4)) bitselector_1 (.in(Dout), .out(Eight_LSB), .sel(1'b0));
  BitSelector #(.group(4)) bitselector_2 (.in(Dout), .out(Eight_MSB), .sel(1'b1));
endmodule

module Datapath (
  input  [15:0] in_1,
  input  in_2,
  input  in_3,
  input  [3:0] AUSel,
  input  [2:0] RUSel,
  input  CLK,
  output [15:0] out_7,
  output [15:0] out_8,
  output [15:0] out_9
);

  wire [7:0] IR_eight_lsb, MAR_result;
  wire [15:0] project_alu_1_audout;

  project_register_16 IR (
    .input_val(project_alu_1_audout), .clk(CLK), .Eight_LSB(IR_eight_lsb));  // open: WE, reset, OE, result, Dout, Eight_MSB
  project_register_16 RegA (
    .input_val(project_alu_1_audout), .clk(CLK), .result(out_8));  // open: WE, reset, OE, Dout, Eight_LSB, Eight_MSB
  project_alu project_alu_1 (
    .A(out_8), .B(out_9), .AUSel(AUSel), .RUSel(RUSel), .AUDout(project_alu_1_audout));  // open: RUResult, AUResult
  project_register_16 RegB (
    .input_val(project_alu_1_audout), .clk(CLK), .result(out_9));  // open: WE, reset, OE, Dout, Eight_LSB, Eight_MSB
  assign project_alu_1_audout = in_2 ? ~in_1 : 16'bz;  // Controlled_Inverter controlled_inverter_1
  assign project_alu_1_audout = in_3 ? ~out_7 : 16'bz;  // Controlled_Inverter controlled_inverter_2
  project_register_16 MBR (
    .input_val(project_alu_1_audout), .clk(CLK), .result(out_7), .Dout(project_alu_1_audout));  // open: WE, reset, OE, Eight_LSB, Eight_MSB
  project_register_8 MAR (
    .input_val(IR_eight_lsb), .clk(CLK), .result(MAR_result));  // open: WE, reset, OE, Dout, Eight_LSB, Eight_MSB
  project_register_16 OutReg (
    .input_val(project_alu_1_audout), .clk(CLK), .result(project_alu_1_audout));  // open: WE, reset, OE, Dout, Eight_LSB, Eight_MSB
endmodule
